# Fritzing sketch Propotype (saved by Fritzing 0.9.3b)
breadboards: 2

parts:
  LCM1602_IIC1 = LCM1602 IIC [part_number="LCM1602 IIC" chip_label="LCM1602 IIC" package="DIP (Dual Inline) [THT]"]
  Mod1 = Raspberry Pi 4B
  LCM1602_IIC2 = LCM1602 IIC [part_number="LCM1602 IIC" chip_label="LCM1602 IIC" package="DIP (Dual Inline) [THT]"]  # not connected
  LCD1 = LCD screen
  hc-sr1 = hc-sr04
  J1 = Basic Servo
  R1 = Resistor [tolerance=±5% resistance=220 package="2010 [SMD]"]

nets:
  VSS: LCM1602_IIC1.VSS, LCD1.VSS
  VDD: LCM1602_IIC1.VDD, LCD1.VDD
  N1: LCM1602_IIC1.V0, LCD1.V0
  N2: LCM1602_IIC1.RS, LCD1.RS
  N3: LCM1602_IIC1.RW, LCD1.R/W
  N4: LCM1602_IIC1.E, LCD1.E
  N5: LCM1602_IIC1.D0, LCD1.DB0
  N6: LCM1602_IIC1.D1, LCD1.DB1
  N7: LCM1602_IIC1.D2, LCD1.DB2
  N8: LCM1602_IIC1.D3, LCD1.DB3
  N9: LCM1602_IIC1.D4, LCD1.DB4
  N10: LCM1602_IIC1.D5, LCD1.DB5
  N11: LCM1602_IIC1.D6, LCD1.DB6
  N12: LCM1602_IIC1.D7, LCD1.DB7
  N13: LCM1602_IIC1.A, LCD1.LED+
  N14: LCM1602_IIC1.K, LCD1.LED-
  GND: LCM1602_IIC1.GND, Mod1.GND, hc-sr1.GND
  VCC: LCM1602_IIC1.VCC, Mod1.3V3
  N15: LCM1602_IIC1.SDA, Mod1.GPIO2
  N16: LCM1602_IIC1.SCL, Mod1.GPIO3
  5V: Mod1.5V, hc-sr1.VCC
  N17: Mod1.GPIO14, hc-sr1.Trig
  N18: Mod1.GPIO15, hc-sr1.Echo
  N19: Mod1.GPIO18, R1.Pin_0
  N20: J1.pulse, R1.Pin_1

notes:
  Ultrasonic sensor
  สายสีแดง VCC 5V
  สายสีดำ GND
  สายสีเหลือง GPIO14 Trig
  สายสีส้ม GPIO15 Echo
  LCD + I2C
  สายสีแดง VCC 5v
  สายสีดำ GND
  สายสีน้ำเงิน SDA
  สายสีเขียว SCL

custom parts:
  LCM1602 IIC: I2C-Module to use a 1602 or 2004 LCD on with the wire.h libory Serial LCD Modul
